# Fritzing sketch practica3 (saved by Fritzing 0.9.1b)
breadboards: 1

parts:
  Parte1 = Arduino Uno (Rev3)
  R2 = Trimmer Potentiometer [maximum_resistance=10kΩ package=THT]
  U1 = LCD-16X2 [package=lcd-16x2_noholes]
  RHT1 = Humidity and Temperature Sensor RHT03
  R3 = Photocell (LDR) [package=THT]
  R4 = Resistor [tolerance=±5% resistance=220 package=THT]

nets:
  N1: Parte1.A0, R3.pin_1, R4.Pin_1
  N2: Parte1.D8, U1.RS
  N3: Parte1.D9_PWM, U1.E
  N4: Parte1.D2, RHT1.Data-signal
  N5: Parte1.D4, U1.DB4
  N6: Parte1.D5_PWM, U1.DB5
  N7: Parte1.D6_PWM, U1.DB6
  N8: Parte1.D7, U1.DB7
  5V: Parte1.5V, R2.wiper, R2.leg2, U1.VDD, U1.A, RHT1.Vcc, R3.pin_0
  GND: Parte1.GND, R2.leg1, U1.VSS, U1.R_W, U1.K, RHT1.GND_2, R4.Pin_0
